# Fritzing sketch Placarduino (saved by Fritzing 0.9.2b)
breadboards: 1

parts:
  LCD1 = LCD screen
  Componente1 = Arduino Uno (Rev3) - ICSP
  R1 = Resistor [tolerance=±5% resistance=300 package=THT]
  R2 = Resistor [tolerance=±5% resistance=1k package=THT]
  S1 = Pushbutton [package="[THT]"]
  S2 = Pushbutton [package="[THT]"]
  R3 = Resistor [tolerance=±5% resistance=10k package=THT]
  R4 = Resistor [tolerance=±5% resistance=10k package=THT]
  Piezo2 = Piezo Speaker
  R5 = Resistor [tolerance=±5% resistance=220 package=THT]

nets:
  GND: LCD1.VSS, LCD1.R/W, LCD1.LED-, Componente1.GND, R2.Pin_0, R3.Pin_0, R4.Pin_0, Piezo2.GND
  VDD: LCD1.VDD, Componente1.5V, R1.Pin_0, S1.Pin_3, S1.Pin_4, S2.Pin_3, S2.Pin_4
  N1: LCD1.V0, R2.Pin_1
  N2: LCD1.RS, Componente1.D13/SCK
  N3: LCD1.E, Componente1.D12/MISO
  N4: LCD1.DB4, Componente1.D11_PWM/MOSI
  N5: LCD1.DB5, Componente1.D10_PWM/SS
  N6: LCD1.DB6, Componente1.D9_PWM
  N7: LCD1.DB7, Componente1.D8
  N8: LCD1.LED+, R1.Pin_1
  N9: Componente1.D5_PWM, R5.Pin_0
  N10: Componente1.D6_PWM, S2.Pin_1, S2.Pin_2, R4.Pin_1
  N11: Componente1.D7, S1.Pin_1, S1.Pin_2, R3.Pin_1
  N12: Piezo2.VCC, R5.Pin_1

custom parts:
  Piezo Speaker: This is a small 12mm round speaker that operates around the audible 2kHz range. You can use these speakers to create simple music or user interfaces.
